# Fritzing sketch Shcematic V1 (saved by Fritzing 0.9.5d)
breadboards: 2

parts:
  Part1 = Arduino Uno (Rev3) - ICSP
  M1 = Getriebemotor
  M2 = Getriebemotor
  M3 = Getriebemotor
  M4 = Getriebemotor
  HC-SR04_Sensor_1 = HC-SR04 Ultrasonic Distance Sensor
  SERVO1 = Tower Pro SG90 servo [part_number=101246]
  Bat1 = battery_holder_single_18650
  Bat2 = battery_holder_single_18650
  J1 = black female 0.1in shorting jumper
  L298N2 = L298N DC motor driver
  J2 = black female 0.1in shorting jumper
  J3 = black female 0.1in shorting jumper
  HC-SR04_Sensor_2 = HC-SR04 Ultrasonic Distance Sensor  # not connected
  SERVO2 = Tower Pro SG90 servo [part_number=101246]  # not connected
  M5 = Getriebemotor  # not connected
  M6 = Getriebemotor  # not connected
  L298N3 = L298N DC motor driver
  J4 = black female 0.1in shorting jumper
  J5 = black female 0.1in shorting jumper
  J6 = black female 0.1in shorting jumper
  Part2 = Arduino Uno (Rev3) - ICSP  # not connected
  Bat3 = battery_holder_single_18650
  Bat5 = battery_holder_single_18650
  J7 = black female 0.1in shorting jumper
  J8 = black female 0.1in shorting jumper
  J9 = black female 0.1in shorting jumper
  SW1 = Slide_Switch_new
  SW2 = Slide_Switch_new  # not connected

nets:
  N1: Part1.D8, L298N2.IN1
  N2: Part1.D9_PWM, L298N2.IN2
  N3: Part1.D10_PWM/SS, L298N2.IN3
  N4: Part1.D11_PWM/MOSI, L298N2.IN4
  N5: Part1.D5_PWM, SERVO1.Signal
  N6: Part1.D6_PWM, HC-SR04_Sensor_1.TRIG
  N7: Part1.D7, HC-SR04_Sensor_1.ECHO
  5V: Part1.5V, HC-SR04_Sensor_1.VCC, SERVO1.+5V, L298N2.5V#7
  GND: Part1.GND, HC-SR04_Sensor_1.GND, SERVO1.GND, Bat2.+#0, L298N2.GND
  N8: M1.pin_1, M2.pin_1, L298N2.OUT4
  N9: M1.pin_2, M2.pin_2, L298N2.OUT3
  N10: M3.pin_1, M4.pin_1, L298N2.OUT1
  N11: M3.pin_2, M4.pin_2, L298N2.OUT2
  N12: Bat1.+#0, Bat2.+#1
  N13: Bat1.+#1, SW1.pin_2
  N14: J1.1, J1.2, L298N2.5VEN, J9.1, J9.2
  N15: L298N2.12V, SW1.pin_1
  N16: L298N2.5V#9, L298N2.ENA, J2.1, J2.2, J8.1, J8.2
  N17: L298N2.5V#10, L298N2.ENB, J3.1, J3.2, J7.1, J7.2
  N18: L298N3.5VEN, J5.1, J5.2
  N19: L298N3.5V#9, L298N3.ENA, J6.1, J6.2
  N20: L298N3.5V#10, L298N3.ENB, J4.1, J4.2
  N21: Bat3.+#0, Bat5.+#1

custom parts:
  Tower Pro SG90 servo: Original file by John De Cristofaro http://www.adafruit.com/products/1449 Adafruit Feedback Servo (Small) Edited by: e-radionica.com 28/9/2015
  battery_holder_single_18650: single 18650 battery holder
  black female 0.1in shorting jumper: black 0.1in female header connection jumper
  L298N DC motor driver: 2x DC motor driver with 78M05 positive voltage regulator (7..35 V) L298N: max 46 V, 2 A Set 5 V Enable jumper to enable 5 V regultor (needed for the L298N) and +5 V output at screw terminal or supply external +5 V at screw terminal Set ENA and/or ENB to +5 V to enable motor permanently or supply ENA and/or ENB with PWM signal IN1 and IN2 set rotation directory for motor A (OUT1/OUT2) IN2 and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
  Slide_Switch_new: the New two pin slide switch

// code stored in the sketch: Schematic Robot Follower V1.ino
#include <Servo.h>


Servo scanServo;


// MOTOR (tetap sama)
int IN1 = 8;
int IN2 = 9;
int IN3 = 10;
int IN4 = 11;


// ULTRASONIC (tetap sama)
int trigPin = 6;
int echoPin = 7;


long duration;
int distance;


// SERVO
int servoPos = 90;
int scanDirection = 1;


bool targetLocked = false;
unsigned long lastScan = 0;


void setup(){


  Serial.begin(9600);


  pinMode(IN1, OUTPUT);
  pinMode(IN2, OUTPUT);
  pinMode(IN3, OUTPUT);
  pinMode(IN4, OUTPUT);


  pinMode(trigPin, OUTPUT);
  pinMode(echoPin, INPUT);


  scanServo.attach(5);
  scanServo.write(90);


  Serial.println("Robot Ready - Migrated Version");
}


// ======================
// ULTRASONIC FILTER
// ======================


int readDistance(){


  const int samples = 8;
  int values[samples];


  for(int i = 0; i < samples; i++){


    digitalWrite(trigPin, LOW);
    delayMicroseconds(2);


    digitalWrite(trigPin, HIGH);
    delayMicroseconds(10);


    digitalWrite(trigPin, LOW);


    duration = pulseIn(echoPin, HIGH, 30000);
    values[i] = duration * 0.034 / 2;


    delay(5);
  }


  int minVal = values[0];
  int maxVal = values[0];
  int sum = 0;


  for(int i = 0; i < samples; i++){


    if(values[i] < minVal) minVal = values[i];
    if(values[i] > maxVal) maxVal = values[i];


    sum += values[i];
  }


  sum -= minVal;
  sum -= maxVal;


  return sum / (samples - 2);
}


// ======================
// MOTOR CONTROL
// ======================


void maju(){


  digitalWrite(IN1, LOW);
  digitalWrite(IN2, HIGH);


  digitalWrite(IN3, LOW);
  digitalWrite(IN4, HIGH);
}


void kiri(){


  digitalWrite(IN1, LOW);
  digitalWrite(IN2, HIGH);


  digitalWrite(IN3, LOW);
  digitalWrite(IN4, LOW);
}


void kanan(){


  digitalWrite(IN1, LOW);
  digitalWrite(IN2, LOW);


  digitalWrite(IN3, LOW);
  digitalWrite(IN4, HIGH);
}


void stopMotor(){


  digitalWrite(IN1, LOW);
  digitalWrite(IN2, LOW);
  digitalWrite(IN3, LOW);
  digitalWrite(IN4, LOW);
}


// ======================
// SERVO SCAN
// ======================


void scanServoSearch(){


  unsigned long now = millis();


  if(now - lastScan > 100){


    servoPos += scanDirection * 8;


    if(servoPos >= 160){
      servoPos = 160;
      scanDirection = -1;
    }


    if(servoPos <= 20){
      servoPos = 20;
      scanDirection = 1;
    }


    scanServo.write(servoPos);
    lastScan = now;
  }
}


// ======================
// MAIN LOOP
// ======================


void loop(){


  distance = readDistance();


  // ignore >40 cm
  if(distance > 40){
    distance = 0;
  }


  Serial.print("Distance: ");
  Serial.print(distance);
  Serial.print(" | Servo: ");
  Serial.println(servoPos);


  if(distance > 5){


    targetLocked = true;


    if(servoPos < 60){
      kiri();
    }


    else if(servoPos > 120){
      kanan();
    }


    else{
      maju();
    }
  }


  else{


    targetLocked = false;
    stopMotor();
  }


  if(!targetLocked){
    scanServoSearch();
  }


  delay(60);
}
